# Fritzing sketch LAYOUT (saved by Fritzing 0.9.3b)
circuit board: 8.46667cm x 5.64444cm
breadboards: 1

parts:
  Bauteil1 = Arduino Nano (Rev3.0)
  Bauteil2 = ws2812b [package="smd 2812b"]
  Bauteil3 = ws2812b [package="smd 2812b"]
  S1 = Pushbutton [package=THT]
  LED1 = LED - 5mm [color="Red (633nm)" package="5 mm [THT]"]
  SG2 = Buzzer 12mm [package=buzzer-12mm-ns]
  U1 = Header 1 [package=1x01_offset]
  U2 = Header 1 [package=1x01_offset]

nets:
  VSS: Bauteil1.GND, Bauteil2.VSS, Bauteil3.VSS, S1.leg0, LED1.cathode, SG2.1, U2.1
  N1: Bauteil1.D2, S1.leg1
  N2: Bauteil1.D3, U1.1
  N3: Bauteil1.D4, Bauteil3.DIN
  N4: Bauteil1.D5, LED1.anode
  N5: Bauteil1.D6, SG2.2
  VDD: Bauteil1.5V, Bauteil2.VDD, Bauteil3.VDD
  N6: Bauteil2.DIN, Bauteil3.DOUT
